// Logisim project 1803078_Lab_5.circ as structural Verilog: 5 circuits, main circuit 5.1.1
module _5_1_1 (
  input  X,
  input  Y,
  output out_3,
  output out_4
);

  wire and_1_out, and_2_out, not_1_out, not_2_out;

  not not_1 (not_1_out, X);
  not not_2 (not_2_out, Y);
  and and_1 (and_1_out, X, not_2_out);
  and and_2 (and_2_out, Y, not_1_out);
  and and_3 (out_4, Y, X);
  or or_1 (out_3, and_1_out, and_2_out);

  // Notes on the sheet:
  //   Experiment no :5.1.1 
  //   Experiment name: Verify the Half Adder Circuit by using Basic gates
  //   S=XY'+X'Y
  //   C=XY
endmodule

module _5_1_2 (
  input  X,
  input  Y,
  output out_3,
  output out_4
);

  wire not_1_out, not_2_out;

  not not_1 (not_1_out, X);
  not not_2 (not_2_out, Y);
  xor xor_1 (out_3, X, Y);
  and and_1 (out_4, Y, X);

  // Notes on the sheet:
  //   Experiment no :5.1.2
  //   Experiment name: Verify the Half Adder Circuit by using XOR gate
  //   S=XY'+X'Y
  //   C=XY
endmodule

module _5_2_1 (
  input  X,
  input  Y,
  input  Z,
  output out_4,
  output C_XY_YZ_ZX
);

  wire and_1_out, and_2_out, and_3_out, and_4_out, and_5_out, and_6_out, and_7_out, not_1_out, not_2_out,
       not_3_out, or_1_out, or_2_out;

  not not_1 (not_1_out, X);
  not not_2 (not_2_out, Y);
  not not_3 (not_3_out, Z);
  and and_1 (and_1_out, not_1_out, not_2_out, Z);
  and and_2 (and_2_out, not_1_out, Y, not_3_out);
  and and_3 (and_3_out, X, not_2_out, not_3_out);
  and and_4 (and_4_out, X, Y, Z);
  and and_5 (and_5_out, X, Y);
  and and_6 (and_6_out, Y, Z);
  and and_7 (and_7_out, Z, X);
  or or_1 (or_1_out, and_1_out, and_2_out);
  or or_2 (or_2_out, and_3_out, and_4_out);
  or or_3 (C_XY_YZ_ZX, and_5_out, and_6_out, and_7_out);
  or or_4 (out_4, or_1_out, or_2_out);

  // Notes on the sheet:
  //   Experiment no :5.2.1
  //   Experiment name: Verify the Full Adder Circuit by SOP
  //   S=X'Y'Z+X'YZ'+XY"Z'+XYZ
endmodule

module _5_2_2 (
  input  X,
  input  Y,
  input  Z,
  output out_4,
  output out_5
);

  wire and_1_out, and_2_out, and_3_out, not_1_out, not_2_out, not_3_out, xor_1_out;

  not not_1 (not_1_out, X);
  not not_2 (not_2_out, Y);
  not not_3 (not_3_out, Z);
  xor xor_1 (xor_1_out, X, Y);
  and and_1 (and_1_out, X, Y);
  and and_2 (and_2_out, Y, Z);
  and and_3 (and_3_out, Z, X);
  xor xor_2 (out_4, xor_1_out, Z);
  or or_1 (out_5, and_1_out, and_2_out, and_3_out);

  // Notes on the sheet:
  //   Experiment no :5.2.2
  //   Experiment name: Verify the Full Adder Circuit by using XOR gate
  //   S
  //   C
endmodule

module _5_3 (
  input  X,
  input  Y,
  input  Z,
  output out_4,
  output C
);

  wire and_1_out, and_2_out, not_1_out, not_2_out, not_3_out, xor_1_out;

  not not_1 (not_1_out, X);
  not not_2 (not_2_out, Y);
  not not_3 (not_3_out, Z);
  xor xor_1 (xor_1_out, X, Y);
  and and_1 (and_1_out, X, Y);
  xor xor_2 (out_4, xor_1_out, Z);
  and and_2 (and_2_out, xor_1_out, Z);
  or or_1 (C, and_2_out, and_1_out);

  // Notes on the sheet:
  //   Experiment no :5.3 
  //   Experiment name: Implement the Full Adder circuit by Half adder circuit and verify the result
  //   S
endmodule
